# Fritzing sketch Sketch (saved by Fritzing 0.8.7b)
breadboards: 1

parts:
  ARDUINO1 = Arduino Micro
  IC1 = '4050 Hex Buffer
  JP1 = Header 8 [package=1x08_smd]
  JP2 = Header 8 [package=1x08_smd]  # not connected

nets:
  3V3: ARDUINO1.3V3, IC1.VCC, JP1.2, JP1.8
  N1: ARDUINO1.GND#31, IC1.VSS, JP1.1
  N2: IC1.G, JP1.7
  N3: IC1.H, JP1.6
  N4: IC1.I, IC1.K, JP1.5
  N5: IC1.L, JP1.4

custom parts:
  Arduino Micro: Arduino Micro Microcontroller
